# Fritzing sketch roboter (saved by Fritzing 0.9.2b)
breadboards: 1

parts:
  Bauteil1 = Arduino Nano (Rev3.0) (ICSP)
  M1 = DC Motor
  VCC1 = Battery block 9V
  M2 = DC Motor
  IC1 = H-Bridge [package=THT]
  R1 = Photocell (LDR) [package=THT]
  R2 = Photocell (LDR) [package=THT]
  R3 = Photocell (LDR) [package=THT]
  R4 = Photocell (LDR) [package=THT]
  R5 = Photocell (LDR) [package=THT]

nets:
  N1: Bauteil1.GND, R1.pin_1, R2.pin_1, R3.pin_1, R4.pin_1, R5.pin_1
  N2: Bauteil1.D5, IC1.4A
  N3: Bauteil1.D6, IC1.3A
  N4: Bauteil1.D7, IC1.1_2EN
  N5: Bauteil1.D8, IC1.3_4EN
  N6: Bauteil1.D9, IC1.2A
  N7: Bauteil1.D10, IC1.1A
  N8: Bauteil1.5V, IC1.VCC1
  N9: Bauteil1.A4, R1.pin_0
  N10: Bauteil1.A3, R2.pin_0
  N11: Bauteil1.A2, R3.pin_0
  N12: Bauteil1.A1, R4.pin_0
  N13: Bauteil1.A0, R5.pin_0
  N14: M1.pin_1, IC1.2Y
  N15: M1.pin_2, IC1.1Y
  GND1: VCC1.-, IC1.GND1, IC1.GND2, IC1.GND3, IC1.GND4
  N16: VCC1.+, IC1.VCC2
  N17: M2.pin_1, IC1.3Y
  N18: M2.pin_2, IC1.4Y
